// Logisim project CS1501_U201514477_华龙_cpu.circ as structural Verilog: 3 circuits, main circuit MIPS CPU
module MIPS_CPU (
);

  wire ALU_Equal, ALU_R_0, and_3_out, and_4_out, and_5_out, beq, bltz, bne, branch, clk, clock_1_out,
       d_ff_1_qn, d_ff_2_qn, d_ff_3_qn, d_ff_4_qn, display__a0, halt, nor_1_out, nor_2_out, not_1_out,
       not_2_out, not_3_out, RST, \单步执行_out ;
  wire [3:0] ALUOP;
  wire [4:0] multiplexer_4_out, multiplexer_8_out, multiplexer_9_out, multiplexer_10_out;
  wire [9:0] PC_q_2;
  wire [15:0] multiplexer_17_out, \总周期数 , \无条件分支指令数 , \有条件分支成功跳转 , \有条件分支指令数 ;
  wire [16:0] multiplexer_5_out, multiplexer_6_out, multiplexer_11_out;
  wire [23:0] alu_1_result_2, control_signal;
  wire [27:2] rom_1_data;
  wire [31:0] bit_extender_1_out, branch_addr, mips_ram_1_p6, multiplexer_1_out, multiplexer_2_out,
       multiplexer_3_out, multiplexer_7_out, multiplexer_12_out, multiplexer_13_out, multiplexer_14_out,
       multiplexer_15_out, multiplexer_16_out, PC_1, PC_q, RF_A, RF_B, SyscallOut;
  wire [31:1] alu_1_result;
  wire [31:26] rom_1_data_2;

  Button \u_总复位  (.out(RST));
  Clock clock_1 (.out(clock_1_out));
  Button \u_单步执行  (.out(\单步执行_out ));
  Multiplexer #(.width(32), .enable("false")) multiplexer_1 (
    .in0(multiplexer_2_out), .in1(multiplexer_3_out), .out(multiplexer_1_out), .sel(control_signal[9]));
  // Probe on multiplexer_1_out
  not not_1 (not_1_out, halt);
  xor xor_1 (clk, clock_1_out, \单步执行_out );
  Multiplexer #(.width(32), .enable("false")) multiplexer_2 (
    .in0(PC_1), .in1(branch_addr), .out(multiplexer_2_out), .sel(branch));
  Multiplexer #(.width(32), .enable("false")) multiplexer_3 (
    .in0({PC_1[31:28], rom_1_data, 2'b00}), .in1(RF_A), .out(multiplexer_3_out), .sel(control_signal[8]));
  PC_1 pc_1_1 (.PC({PC_q[31:12], PC_q_2, PC_q[1:0]}), .PC_4(PC_1));
  Register #(.width(32)) PC (
    .D(multiplexer_1_out), .en(not_1_out), .Q({PC_q[31:12], PC_q_2, PC_q[1:0]}), .clk(clk), .clr(RST));
  Hex_Digit_Display hex_digit_display_1 (.value(SyscallOut[27:24]));  // open: dp
  Hex_Digit_Display hex_digit_display_2 (.value(SyscallOut[31:28]));  // open: dp
  Register #(.width(32)) \u_数码管锁存  (.D(RF_B), .en(display__a0), .Q(SyscallOut), .clk(clk), .clr(RST));
  Hex_Digit_Display hex_digit_display_3 (.value(SyscallOut[19:16]));  // open: dp
  Hex_Digit_Display hex_digit_display_4 (.value(SyscallOut[23:20]));  // open: dp
  ROM #(.addrWidth(10), .dataWidth(32)) rom_1 (.addr(PC_q_2), .data({rom_1_data_2, rom_1_data}));  // open: sel
  Hex_Digit_Display hex_digit_display_5 (.value(SyscallOut[15:12]));  // open: dp
  Hex_Digit_Display hex_digit_display_6 (.value(SyscallOut[11:8]));  // open: dp
  MIPS_Controller mips_controller_1 (
    .OP(rom_1_data_2), .Funct(rom_1_data[7:2]),
    .\控制信号 ({ALUOP, control_signal[23:8], beq, bne, bltz, control_signal[4:0]}));
  Hex_Digit_Display hex_digit_display_7 (.value(SyscallOut[7:4]));  // open: dp
  Hex_Digit_Display hex_digit_display_8 (.value(SyscallOut[3:0]));  // open: dp
  Multiplexer #(.width(5), .enable("false")) multiplexer_4 (
    .in0(rom_1_data[22:18]), .in1(rom_1_data[17:13]), .out(multiplexer_4_out), .sel(control_signal[21]));
  Multiplexer #(.width(17), .enable("false")) multiplexer_5 (
    .in0(17'ha), .in1({{12{1'b0}}, rom_1_data[12:8]}), .out(multiplexer_5_out), .sel(control_signal[12]));
  Multiplexer #(.width(17), .enable("false")) multiplexer_6 (
    .in0({{2{rom_1_data[17]}}, rom_1_data[16:2]}), .in1({1'b0, rom_1_data[17:2]}), .out(multiplexer_6_out),
    .sel(control_signal[10]));
  Multiplexer #(.width(32), .enable("false")) multiplexer_7 (
    .in0(multiplexer_12_out), .in1(multiplexer_13_out), .out(multiplexer_7_out), .sel(control_signal[17]));
  Multiplexer #(.width(5), .enable("false")) multiplexer_8 (
    .in0(rom_1_data[27:23]), .in1(5'b00010), .out(multiplexer_8_out), .sel(control_signal[23]));
  Multiplexer #(.width(5), .enable("false")) multiplexer_9 (
    .in0(rom_1_data[22:18]), .in1(5'b00100), .out(multiplexer_9_out), .sel(control_signal[22]));
  Multiplexer #(.width(5), .enable("false")) multiplexer_10 (
    .in0(multiplexer_4_out), .in1({5{1'b1}}), .out(multiplexer_10_out), .sel(control_signal[20]));
  Multiplexer #(.width(17), .enable("false")) multiplexer_11 (
    .in0(multiplexer_5_out), .in1(multiplexer_6_out), .out(multiplexer_11_out), .sel(control_signal[11]));
  Multiplexer #(.width(32), .enable("false")) multiplexer_12 (
    .in0({alu_1_result[31:26], alu_1_result_2, alu_1_result[1], ALU_R_0}), .in1(PC_1),
    .out(multiplexer_12_out), .sel(control_signal[18]));
  Multiplexer #(.width(32), .enable("false")) multiplexer_13 (
    .in0(mips_ram_1_p6), .in1({{16{1'b0}}, multiplexer_17_out}), .out(multiplexer_13_out),
    .sel(control_signal[16]));
  // Probe on multiplexer_10_out
  assign bit_extender_1_out = {{15{multiplexer_11_out[16]}}, multiplexer_11_out};  // Bit_Extender bit_extender_1
  // Probe on \总周期数 
  // Probe on \无条件分支指令数 
  // Probe on \有条件分支指令数 
  // Probe on \有条件分支成功跳转 
  // RegisterFile registerfile_1: pin names not known; wires that end beside it: multiplexer_7_out, clk, control_signal[19], multiplexer_10_out, multiplexer_8_out, multiplexer_9_out, RF_A, RF_B
  // Probe on multiplexer_9_out
  // Probe on multiplexer_8_out
  Multiplexer #(.width(32), .enable("false")) multiplexer_14 (
    .in0(RF_B), .in1(RF_A), .out(multiplexer_14_out), .sel(control_signal[14]));
  Adder #(.width(32)) adder_1 (.a(PC_1), .b({bit_extender_1_out[29:0], 2'b00}), .out(branch_addr));  // open: cin, cout
  Multiplexer #(.width(32), .enable("false")) multiplexer_15 (
    .in0(RF_A), .in1(RF_B), .out(multiplexer_15_out), .sel(control_signal[15]));
  ALU alu_1 (
    .AluOP(ALUOP), .X(multiplexer_15_out), .Equal(ALU_Equal),
    .Result({alu_1_result[31:26], alu_1_result_2, alu_1_result[1], ALU_R_0}), .Y(multiplexer_16_out));  // open: Signed_Overflow, Result_2, UnSigned_Overflow
  Multiplexer #(.width(32), .enable("false")) multiplexer_16 (
    .in0(multiplexer_14_out), .in1(bit_extender_1_out), .out(multiplexer_16_out), .sel(control_signal[13]));
  // MIPS_RAM mips_ram_1: pin names not known; wires that end beside it: alu_1_result_2, RF_B, control_signal[3], clk, RST, mips_ram_1_p6
  Multiplexer #(.width(16), .enable("false")) multiplexer_17 (
    .in0(mips_ram_1_p6[15:0]), .in1(mips_ram_1_p6[31:16]), .out(multiplexer_17_out), .sel(alu_1_result[1]));
  nor nor_1 (nor_1_out, control_signal[9], control_signal[8]);
  nor nor_2 (nor_2_out, beq, bne, bltz);
  not not_2 (not_2_out, branch);
  not not_3 (not_3_out, ALU_Equal);
  D_Flip_Flop d_ff_1 (.clk(clk), .D(halt), .Qn(d_ff_1_qn), .reset(RST));  // open: Q, preset, en
  D_Flip_Flop d_ff_2 (.clk(clk), .D(nor_1_out), .Qn(d_ff_2_qn), .preset(RST));  // open: Q, en, reset
  D_Flip_Flop d_ff_3 (.clk(clk), .D(nor_2_out), .Qn(d_ff_3_qn), .preset(RST));  // open: Q, en, reset
  D_Flip_Flop d_ff_4 (.clk(clk), .D(not_2_out), .Qn(d_ff_4_qn), .preset(RST));  // open: Q, en, reset
  and and_1 (halt, control_signal[4], ~not_3_out);  // AND_Gate
  and and_2 (display__a0, control_signal[4], not_3_out);
  and and_3 (and_3_out, ALU_Equal, beq);
  or or_1 (branch, and_3_out, and_4_out, and_5_out);
  and and_4 (and_4_out, ~ALU_Equal, bne);  // AND_Gate
  and and_5 (and_5_out, ALU_R_0, bltz);
  Counter #(.width(16), .max('hffff)) \u_总周期计数  (
    .count(d_ff_1_qn), .Q(\总周期数 ), .clk(clk), .clr(RST));  // open: load, D, carry
  Counter #(.width(16), .max('hffff)) \u_无条件分支指令计数  (
    .count(d_ff_2_qn), .Q(\无条件分支指令数 ), .clk(clk), .clr(RST));  // open: load, D, carry
  Counter #(.width(16), .max('hffff)) \u_有条件分支指令计数  (
    .count(d_ff_3_qn), .Q(\有条件分支指令数 ), .clk(clk), .clr(RST));  // open: load, D, carry
  Counter #(.width(16), .max('hffff)) \u_有条件分支成功跳转计数  (
    .count(d_ff_4_qn), .Q(\有条件分支成功跳转 ), .clk(clk), .clr(RST));  // open: load, D, carry

  // Other names for the same wires on the sheet: DM_WE = control_signal[3]; syscall = control_signal[4];
  //   control_signal (some bits) = {ALUOP, beq, bne, bltz}; jump_register = control_signal[8];
  //   jump = control_signal[9]; zero_ext_IMM = control_signal[10]; extend_IMM = control_signal[11];
  //   extend_shamt = control_signal[12]; Y__S_EXT = control_signal[13]; Y__RF_A = control_signal[14];
  //   X__RF_B = control_signal[15]; Din__DM_half = control_signal[16]; Din__DM = control_signal[17];
  //   Din__PC_1 = control_signal[18]; RF_WE = control_signal[19]; rW__GPR_31 = control_signal[20];
  //   rW__rd = control_signal[21]; rB___a0 = control_signal[22]; rA___v0 = control_signal[23]

  // Notes on the sheet:
  //   数码管输出应该用寄存器锁存，否则显示数据只能一闪而过
  //   指令存储器
  //   可以通过项目增加Logisim库的方式将前几次实验完成的电路作为子电路引入到本电路中使用
  //   contents of rom_1 (hex, n*v repeats v):
  //   20110001 8000c05 20110001 20120002 20130003 8000c09 20110001 20120002 20130003 8000c0d 20110001
  //   20120002 20130003 8000c11 20110001 20120002 20130003 c000cb8 20100001 20110001 118fc0 112020
  //   20020022 c 118882 12200001 8000c15 112020 20020022 c 20110001 118880 112020 20020022 c 12200001
  //   8000c1f 20110001 118fc0 112020 20020022 c 1188c3 112020 20020022 c 118903 112020 20020022 c 118903
  //   112020 20020022 c 118903 112020 20020022 c 118903 112020 20020022 c 118903 112020 20020022 c 118903
  //   112020 20020022 c 118903 112020 20020022 c 20100001 109fc0 139fc3 8021 2012000c 24160003 26100001
  //   3210000f 20080008 20090001 139900 2709825 132020 20020022 c 1094022 1500fff9 22100001 2018000f
  //   2188024 108700 20080008 20090001 139902 2709825 132021 20020022 c 1094022 1500fff9 108702 2c9b022
  //   12c00001 8000c50 4020 1084027 84400 3508ffff 82021 20020022 c 2010ffff 20110000 ae300000 22100001
  //   22310004 ae300000 22100001 22310004 ae300000 22100001 22310004 ae300000 22100001 22310004 ae300000
  //   22100001 22310004 ae300000 22100001 22310004 ae300000 22100001 22310004 ae300000 22100001 22310004
  //   ae300000 22100001 22310004 ae300000 22100001 22310004 ae300000 22100001 22310004 ae300000 22100001
  //   22310004 ae300000 22100001 22310004 ae300000 22100001 22310004 ae300000 22100001 22310004 ae300000
  //   22100001 22310004 22100001 8020 2011003c 8e130000 8e340000 274402a 11000002 ae330000 ae140000
  //   2231fffc 1611fff8 102020 20020022 c 22100004 2011003c 1611fff2 2002000a c 20100000 22100001 102020
  //   20020022 c 22100002 102020 20020022 c 22100003 102020 20020022 c 22100004 102020 20020022 c 22100005
  //   102020 20020022 c 22100006 102020 20020022 c 22100007 102020 20020022 c 22100008 102020 20020022
  //   20020022 c 3e00008
  //   数码管输出
  //   总复位信号应将除ROM以外所有存储组件全部清零
  //   寄存器堆
  //   数据存储器
endmodule

module PC_1 (
  input  [31:0] PC,
  output [31:0] PC_4
);

  // Incrementer incrementer_1: pin names not known; wires that end beside it: PC[31:2], PC_4[31:2]

  assign PC_4[1:0] = PC[1:0];
endmodule

module MIPS_Controller (
  input  [5:0] OP,
  input  [5:0] Funct,
  output [27:0] \控制信号 
);

  wire comparator_1_eq, comparator_2_eq, comparator_3_eq, comparator_4_eq, comparator_5_eq, comparator_6_eq,
       comparator_7_eq, comparator_8_eq, comparator_9_eq, comparator_10_eq, comparator_11_eq,
       comparator_12_eq, comparator_13_eq, comparator_14_eq, comparator_15_eq, comparator_16_eq,
       comparator_17_eq, comparator_18_eq, comparator_19_eq, comparator_20_eq, comparator_21_eq,
       comparator_22_eq, comparator_23_eq, comparator_24_eq, comparator_25_eq, comparator_26_eq,
       comparator_27_eq, comparator_28_eq, comparator_29_eq;
  wire [3:0] priority_encoder_1_out, priority_encoder_2_out;
  wire [27:0] multiplexer_1_out;

  Comparator #(.width(6)) comparator_1 (.a(OP), .b({6{1'b0}}), .eq(comparator_1_eq));  // open: gt, lt
  Comparator #(.width(6)) comparator_2 (.a(OP), .b(6'b000001), .eq(comparator_2_eq));  // open: gt, lt
  Comparator #(.width(6)) comparator_3 (.a(OP), .b(6'b000010), .eq(comparator_3_eq));  // open: gt, lt
  Comparator #(.width(6)) comparator_4 (.a(OP), .b(6'b000011), .eq(comparator_4_eq));  // open: gt, lt
  Comparator #(.width(6)) comparator_5 (.a(OP), .b(6'b000100), .eq(comparator_5_eq));  // open: gt, lt
  Comparator #(.width(6)) comparator_6 (.a(OP), .b(6'b000101), .eq(comparator_6_eq));  // open: gt, lt
  Comparator #(.width(6)) comparator_7 (.a(OP), .b(6'b001000), .eq(comparator_7_eq));  // open: gt, lt
  Comparator #(.width(6)) comparator_8 (.a(OP), .b(6'b001001), .eq(comparator_8_eq));  // open: gt, lt
  Comparator #(.width(6)) comparator_9 (.a(OP), .b(6'b001010), .eq(comparator_9_eq));  // open: gt, lt
  Comparator #(.width(6)) comparator_10 (.a(OP), .b(6'b001011), .eq(comparator_10_eq));  // open: gt, lt
  Comparator #(.width(6)) comparator_11 (.a(OP), .b(6'b001100), .eq(comparator_11_eq));  // open: gt, lt
  Comparator #(.width(6)) comparator_12 (.a(OP), .b(6'b001101), .eq(comparator_12_eq));  // open: gt, lt
  Comparator #(.width(6)) comparator_13 (.a(OP), .b(6'b100001), .eq(comparator_13_eq));  // open: gt, lt
  Comparator #(.width(6)) comparator_14 (.a(OP), .b(6'b100011), .eq(comparator_14_eq));  // open: gt, lt
  Comparator #(.width(6)) comparator_15 (.a(OP), .b(6'b101011), .eq(comparator_15_eq));  // open: gt, lt
  Priority_Encoder #(.select(4), .disabled(0)) priority_encoder_1 (
    .in0(1'b1), .in1(comparator_1_eq), .in2(comparator_2_eq), .in3(comparator_3_eq), .in4(comparator_4_eq),
    .in5(comparator_5_eq), .in6(comparator_6_eq), .in7(comparator_7_eq), .in8(comparator_8_eq),
    .in9(comparator_9_eq), .in10(comparator_10_eq), .in11(comparator_11_eq), .in12(comparator_12_eq),
    .in13(comparator_13_eq), .in14(comparator_14_eq), .in15(comparator_15_eq), .out(priority_encoder_1_out));  // open: gs, en_out, en_in
  Comparator #(.width(6)) comparator_16 (.a(Funct), .b({6{1'b0}}), .eq(comparator_16_eq));  // open: gt, lt
  Comparator #(.width(6)) comparator_17 (.a(Funct), .b(6'b000010), .eq(comparator_17_eq));  // open: gt, lt
  Comparator #(.width(6)) comparator_18 (.a(Funct), .b(6'b000011), .eq(comparator_18_eq));  // open: gt, lt
  Comparator #(.width(6)) comparator_19 (.a(Funct), .b(6'b000110), .eq(comparator_19_eq));  // open: gt, lt
  Comparator #(.width(6)) comparator_20 (.a(Funct), .b(6'b001000), .eq(comparator_20_eq));  // open: gt, lt
  Comparator #(.width(6)) comparator_21 (.a(Funct), .b(6'b001100), .eq(comparator_21_eq));  // open: gt, lt
  Comparator #(.width(6)) comparator_22 (.a(Funct), .b(6'b100000), .eq(comparator_22_eq));  // open: gt, lt
  Comparator #(.width(6)) comparator_23 (.a(Funct), .b(6'b100001), .eq(comparator_23_eq));  // open: gt, lt
  Comparator #(.width(6)) comparator_24 (.a(Funct), .b(6'b100010), .eq(comparator_24_eq));  // open: gt, lt
  Comparator #(.width(6)) comparator_25 (.a(Funct), .b(6'b100100), .eq(comparator_25_eq));  // open: gt, lt
  Comparator #(.width(6)) comparator_26 (.a(Funct), .b(6'b100101), .eq(comparator_26_eq));  // open: gt, lt
  Comparator #(.width(6)) comparator_27 (.a(Funct), .b(6'b100111), .eq(comparator_27_eq));  // open: gt, lt
  Comparator #(.width(6)) comparator_28 (.a(Funct), .b(6'b101010), .eq(comparator_28_eq));  // open: gt, lt
  Comparator #(.width(6)) comparator_29 (.a(Funct), .b(6'b101011), .eq(comparator_29_eq));  // open: gt, lt
  Priority_Encoder #(.select(4), .disabled(0)) priority_encoder_2 (
    .in0(1'b1), .in1(1'b0), .in2(comparator_16_eq), .in3(comparator_17_eq), .in4(comparator_18_eq),
    .in5(comparator_19_eq), .in6(comparator_20_eq), .in7(comparator_21_eq), .in8(comparator_22_eq),
    .in9(comparator_23_eq), .in10(comparator_24_eq), .in11(comparator_25_eq), .in12(comparator_26_eq),
    .in13(comparator_27_eq), .in14(comparator_28_eq), .in15(comparator_29_eq), .out(priority_encoder_2_out));  // open: gs, en_out, en_in
  Multiplexer #(.select(4), .width(28), .disabled(0), .enable("false")) multiplexer_1 (
    .in0({28{1'b0}}), .in1({28{1'b0}}), .in2(28'h28b000), .in3(28'h228b000), .in4(28'h128b000),
    .in5(28'h228c000), .in6(28'h300), .in7(28'h6c02010), .in8(28'h5280000), .in9(28'h5280000),
    .in10(28'h6280000), .in11(28'h7280000), .in12(28'h8280000), .in13(28'ha280000), .in14(28'hb280000),
    .in15(28'hc280000), .out(multiplexer_1_out), .sel(priority_encoder_2_out));
  Multiplexer #(.select(4), .width(28), .disabled(0), .enable("false")) multiplexer_2 (
    .in0({28{1'b0}}), .in1(multiplexer_1_out), .in2(28'hb000820), .in3(28'h200), .in4(28'h1c0200),
    .in5(28'h880), .in6(28'h840), .in7(28'h5082800), .in8(28'h5082800), .in9(28'hb082800),
    .in10(28'hc082800), .in11(28'h7082c00), .in12(28'h8082c00), .in13(28'h50b2800), .in14(28'h50a2800),
    .in15(28'h5002808), .out(\控制信号 ), .sel(priority_encoder_1_out));
endmodule
